// Logisim project 18b MIPS ISA Group 4 .circ as structural Verilog: 4 circuits, main circuit MIPS Datapath with control unit for project
module MIPS_Datapath_with_control_unit_for_project (
  input  mem_clr,
  input  reg_clear,
  output [17:0] result,
  output cout
);

  wire and_1_out, control_unit_for_project_1_alu_src, control_unit_for_project_1_beq,
       control_unit_for_project_1_cin, control_unit_for_project_1_jump, control_unit_for_project_1_load,
       control_unit_for_project_1_mem_enable, control_unit_for_project_1_memtoreg,
       control_unit_for_project_1_reg_dest, control_unit_for_project_1_store, control_unit_for_project_1_wc,
       Master_Clk_out, n18_bit_alu_for_project_1_zero_flag, PC_Clr_out;
  wire [1:0] rom_1_data_2;
  wire [2:0] multiplexer_1_out, rom_1_data_3, rom_1_data_6, rom_1_data_7;
  wire [3:0] bit_extender_1_out, bit_extender_2_out, control_unit_for_project_1_alu_op, rom_1_data_4;
  wire [3:2] rom_1_data;
  wire [4:4] rom_1_data_5;
  wire [17:0] adder_1_out, adder_2_out, bit_extender_3_out, bit_extender_4_out, multiplexer_2_out,
       multiplexer_3_out, multiplexer_4_out, multiplexer_5_out,
       n18_bit_7_register_file_for_project_1_read_data_1, n18_bit_7_register_file_for_project_1_read_data_2,
       n18_bit_alu_for_project_1_result, PC_q, ram_1_data;

  Hex_Digit_Display hex_digit_display_1 (.value(multiplexer_4_out[15:12]));  // open: dp
  Hex_Digit_Display hex_digit_display_2 (.value(bit_extender_1_out));  // open: dp
  assign bit_extender_1_out = {{2{1'b0}}, multiplexer_4_out[17:16]};  // Bit_Extender bit_extender_1
  Hex_Digit_Display hex_digit_display_3 (.value({rom_1_data, rom_1_data_7[2:1]}));  // open: dp
  Hex_Digit_Display hex_digit_display_4 (.value(bit_extender_2_out));  // open: dp
  assign bit_extender_2_out = {{2{1'b0}}, rom_1_data_2};  // Bit_Extender bit_extender_2
  Hex_Digit_Display hex_digit_display_5 (.value(multiplexer_4_out[11:8]));  // open: dp
  Hex_Digit_Display hex_digit_display_6 (.value(multiplexer_4_out[7:4]));  // open: dp
  Hex_Digit_Display hex_digit_display_7 (.value({rom_1_data_6, rom_1_data_5[4]}));  // open: dp
  Hex_Digit_Display hex_digit_display_8 (.value({rom_1_data_7[0], rom_1_data_3}));  // open: dp
  Hex_Digit_Display hex_digit_display_9 (.value(multiplexer_4_out[3:0]));  // open: dp
  Hex_Digit_Display hex_digit_display_10 (.value(rom_1_data_4));  // open: dp
  Clock Master_Clk (.out(Master_Clk_out));
  Button PC_Clr (.out(PC_Clr_out));
  assign bit_extender_3_out = {{17{1'b0}}, 1'b1};  // Bit_Extender bit_extender_3
  Register #(.width(18)) PC (.D(multiplexer_5_out), .Q(PC_q), .clk(Master_Clk_out), .clr(PC_Clr_out));  // open: en
  Adder #(.width(18)) adder_1 (.a(PC_q), .b(bit_extender_3_out), .out(adder_1_out));  // open: cin, cout
  assign bit_extender_4_out = {{4{1'b0}}, {rom_1_data_7, rom_1_data_3, rom_1_data_6, rom_1_data_5[4], rom_1_data_4}};  // Bit_Extender bit_extender_4
  ROM #(.addrWidth(18), .dataWidth(18)) rom_1 (
    .addr(PC_q),
    .data({rom_1_data_2, rom_1_data, rom_1_data_7, rom_1_data_3, rom_1_data_6, rom_1_data_5[4], rom_1_data_4}));  // open: sel
  control_unit_for_project control_unit_for_project_1 (
    .opcode({rom_1_data_2, rom_1_data}), .Function_bit(rom_1_data_4),
    .ALU_OP(control_unit_for_project_1_alu_op), .CIN(control_unit_for_project_1_cin),
    .Reg_Dest(control_unit_for_project_1_reg_dest), .ALU_src(control_unit_for_project_1_alu_src),
    .MemToReg(control_unit_for_project_1_memtoreg), .WC(control_unit_for_project_1_wc),
    .Load(control_unit_for_project_1_load), .Store(control_unit_for_project_1_store),
    .Mem_Enable(control_unit_for_project_1_mem_enable), .BEQ(control_unit_for_project_1_beq),
    .JUMP(control_unit_for_project_1_jump));
  assign result = {{10{1'b0}}, {rom_1_data_6, rom_1_data_5[4], rom_1_data_4}};  // Bit_Extender bit_extender_5
  Multiplexer #(.width(3), .enable("false")) multiplexer_1 (
    .in0(rom_1_data_6), .in1(rom_1_data_3), .out(multiplexer_1_out), .sel(control_unit_for_project_1_reg_dest));
  _18_bit_7_register_file_for_project u_18_bit_7_register_file_for_project_1 (
    .write_register(multiplexer_1_out), .Write_data(multiplexer_4_out),
    .enable_write_control(control_unit_for_project_1_wc), .CLOCK(Master_Clk_out), .clr(reg_clear),
    .Rs1(rom_1_data_7), .Rs2(rom_1_data_3), .read_data_2(n18_bit_7_register_file_for_project_1_read_data_2),
    .read_data_1(n18_bit_7_register_file_for_project_1_read_data_1));
  Multiplexer #(.width(18), .enable("false")) multiplexer_2 (
    .in0(n18_bit_7_register_file_for_project_1_read_data_2), .in1(result), .out(multiplexer_2_out),
    .sel(control_unit_for_project_1_alu_src));
  Adder #(.width(18)) adder_2 (.a(adder_1_out), .b(result), .out(adder_2_out));  // open: cin, cout
  _18_bit_alu_for_project u_18_bit_alu_for_project_1 (
    .A(n18_bit_7_register_file_for_project_1_read_data_1), .B(multiplexer_2_out),
    .cin(control_unit_for_project_1_cin), .Selection_bit(control_unit_for_project_1_alu_op),
    .result(n18_bit_alu_for_project_1_result), .Zero_Flag(n18_bit_alu_for_project_1_zero_flag), .cout(cout));
  and and_1 (and_1_out, control_unit_for_project_1_beq, n18_bit_alu_for_project_1_zero_flag);
  Multiplexer #(.width(18), .enable("false")) multiplexer_3 (
    .in0(adder_1_out), .in1(adder_2_out), .out(multiplexer_3_out), .sel(and_1_out));
  Multiplexer #(.width(18), .enable("false")) multiplexer_4 (
    .in0(n18_bit_alu_for_project_1_result), .in1(ram_1_data), .out(multiplexer_4_out),
    .sel(control_unit_for_project_1_memtoreg));
  RAM #(.addrWidth(18), .dataWidth(18), .bus("separate")) ram_1 (
    .addr(n18_bit_alu_for_project_1_result), .din(n18_bit_7_register_file_for_project_1_read_data_2),
    .data(ram_1_data), .str(control_unit_for_project_1_store), .sel(control_unit_for_project_1_mem_enable),
    .clk(Master_Clk_out), .ld(control_unit_for_project_1_load), .clr(mem_clr));
  Multiplexer #(.width(18), .enable("false")) multiplexer_5 (
    .in0(multiplexer_3_out), .in1(bit_extender_4_out), .out(multiplexer_5_out),
    .sel(control_unit_for_project_1_jump));

  // Notes on the sheet:
  //   Write Data
  //   Instruction Data
  //   Complete Datapath 18 Bits MIPS ISA
  //   Atahar Hossain 2231877642
  //   Sadman Sakib 2232058042
  //   without opcode
  //   contents of rom_1 (hex, n*v repeats v):
  //   3562 24402 c409 5 11403 1a604 6309 20001 20001
  //   function bit
  //   rd 
  //   rt
  //   opcode
  //   immediete
  //   rs
  //   BEQ
  //   Jump
endmodule

module _18_bit_7_register_file_for_project (
  input  [2:0] write_register,
  input  [17:0] Write_data,
  input  enable_write_control,
  input  CLOCK,
  input  clr,
  input  [2:0] Rs2,
  input  [2:0] Rs1,
  output [17:0] read_data_1,
  output [17:0] read_data_2
);

  wire and_1_out, and_2_out, and_3_out, and_4_out, and_5_out, and_6_out, and_7_out, and_8_out,
       decoder_1_out0, decoder_1_out1, decoder_1_out2, decoder_1_out3, decoder_1_out4, decoder_1_out5,
       decoder_1_out6, decoder_1_out7;
  wire [17:0] R0_q, R1_q, R2_q, R3_q, R4_q, R5_q, R6_q, R7_q;

  Decoder #(.select(3)) decoder_1 (
    .out0(decoder_1_out0), .out1(decoder_1_out1), .out2(decoder_1_out2), .out3(decoder_1_out3),
    .out4(decoder_1_out4), .out5(decoder_1_out5), .out6(decoder_1_out6), .out7(decoder_1_out7),
    .sel(write_register));  // open: en
  and and_1 (and_1_out, decoder_1_out0, enable_write_control);
  and and_2 (and_2_out, decoder_1_out1, enable_write_control);
  and and_3 (and_3_out, decoder_1_out2, enable_write_control);
  and and_4 (and_4_out, decoder_1_out3, enable_write_control);
  and and_5 (and_5_out, decoder_1_out4, enable_write_control);
  and and_6 (and_6_out, decoder_1_out5, enable_write_control);
  and and_7 (and_7_out, decoder_1_out6, enable_write_control);
  and and_8 (and_8_out, decoder_1_out7, enable_write_control);
  Register #(.width(18)) R0 (.D(Write_data), .en(and_1_out), .Q(R0_q), .clk(CLOCK), .clr(clr));
  Register #(.width(18)) R1 (.D(Write_data), .en(and_2_out), .Q(R1_q), .clk(CLOCK), .clr(clr));
  Register #(.width(18)) R2 (.D(Write_data), .en(and_3_out), .Q(R2_q), .clk(CLOCK), .clr(clr));
  Register #(.width(18)) R3 (.D(Write_data), .en(and_4_out), .Q(R3_q), .clk(CLOCK), .clr(clr));
  Register #(.width(18)) R4 (.D(Write_data), .en(and_5_out), .Q(R4_q), .clk(CLOCK), .clr(clr));
  Register #(.width(18)) R5 (.D(Write_data), .en(and_6_out), .Q(R5_q), .clk(CLOCK), .clr(clr));
  Register #(.width(18)) R6 (.D(Write_data), .en(and_7_out), .Q(R6_q), .clk(CLOCK), .clr(clr));
  Register #(.width(18)) R7 (.D(Write_data), .en(and_8_out), .Q(R7_q), .clk(CLOCK), .clr(clr));
  Multiplexer #(.select(3), .width(18)) multiplexer_1 (
    .in0(R0_q), .in1(R1_q), .in2(R2_q), .in3(R3_q), .in4(R4_q), .in5(R5_q), .in6(R6_q), .in7(R7_q),
    .out(read_data_1), .sel(Rs1));  // open: en
  Multiplexer #(.select(3), .width(18)) multiplexer_2 (
    .in0(R0_q), .in1(R1_q), .in2(R2_q), .in3(R3_q), .in4(R4_q), .in5(R5_q), .in6(R6_q), .in7(R7_q),
    .out(read_data_2), .sel(Rs2));  // open: en

  // Notes on the sheet:
  //   18 bit Register File
  //   Atahar Hossain 2231877642
  //   Sadman Sakib 2232058042
endmodule

module control_unit_for_project (
  input  [3:0] Function_bit,
  input  [3:0] opcode,
  output [3:0] ALU_OP,
  output CIN,
  output Reg_Dest,
  output ALU_src,
  output MemToReg,
  output WC,
  output Load,
  output Store,
  output Mem_Enable,
  output BEQ,
  output JUMP
);

  wire decoder_1_out0, decoder_1_out2, decoder_1_out5, decoder_1_out6, decoder_1_out7, decoder_1_out10,
       decoder_1_out11, decoder_1_out12, decoder_1_out13, decoder_1_out14, decoder_1_out15, OR_out;
  wire [3:0] multiplexer_1_out;

  or OR (OR_out, opcode[3], opcode[2], opcode[1], opcode[0]);
  Multiplexer #(.width(4)) multiplexer_1 (
    .in0(Function_bit), .in1(opcode), .out(multiplexer_1_out), .sel(OR_out));  // open: en
  Decoder #(.select(4)) decoder_1 (
    .out0(decoder_1_out0), .out1(CIN), .out2(decoder_1_out2), .out3(Store), .out4(BEQ),
    .out5(decoder_1_out5), .out6(decoder_1_out6), .out7(decoder_1_out7), .out8(JUMP), .out9(Load),
    .out10(decoder_1_out10), .out11(decoder_1_out11), .out12(decoder_1_out12), .out13(decoder_1_out13),
    .out14(decoder_1_out14), .out15(decoder_1_out15), .sel(multiplexer_1_out));  // open: en
  or or_2 (ALU_OP[0], CIN, Store, decoder_1_out5, decoder_1_out7, Load);
  or or_3 (ALU_OP[1], decoder_1_out2, Store, decoder_1_out6, decoder_1_out7, decoder_1_out10);
  or or_4 (ALU_OP[2], BEQ, decoder_1_out5, decoder_1_out6, decoder_1_out7);
  or or_5 (ALU_OP[3], JUMP, Load, decoder_1_out10);
  or or_6 (Reg_Dest, CIN, Store, BEQ, decoder_1_out6, Load);
  or or_7 (ALU_src, CIN, Store, decoder_1_out6, Load);
  or or_8 (Mem_Enable, Store, Load);
  or or_9 (WC, CIN, decoder_1_out2, decoder_1_out7, decoder_1_out6, Load, decoder_1_out10);

  assign MemToReg = Load;

  // Notes on the sheet:
  //   Control Unit
  //   Atahar Hossain 2231877642
  //   Sadman Sakib 2232058042
endmodule

module _18_bit_alu_for_project (
  input  [3:0] Selection_bit,
  input  [17:0] A,
  input  [17:0] B,
  input  cin,
  output [17:0] result,
  output Zero_Flag,
  output cout
);

  wire adder_1_cout, adder_2_cout, comparator_1_eq, comparator_1_gt, comparator_1_lt, nor_1_out, OR_2_out,
       or_3_out;
  wire [4:0] bit_extender_1_out;
  wire [17:0] adder_1_out, adder_2_out, ANDi_out, multiplexer_1_out, not_1_out, OR_out, shifter_1_out;

  assign ANDi_out = B & A;  // AND_Gate ANDi, 18 bits wide
  assign OR_out = B | A;  // OR_Gate OR, 18 bits wide
  Multiplexer #(.width(18)) multiplexer_1 (
    .in0(B), .in1(not_1_out), .out(multiplexer_1_out), .sel(Selection_bit[0]));  // open: en
  assign not_1_out = ~B;  // NOT_Gate not_1, 18 bits wide
  Bit_Extender #(.in_width(18), .out_width(5)) bit_extender_1 (.in(B), .out(bit_extender_1_out));
  Shifter #(.width(18)) shifter_1 (.in(A), .\dist (bit_extender_1_out), .out(shifter_1_out));
  Comparator #(.width(18)) comparator_1 (
    .a(A), .b(B), .gt(comparator_1_gt), .eq(comparator_1_eq), .lt(comparator_1_lt));
  Adder #(.width(18)) adder_1 (.a(A), .b(multiplexer_1_out), .out(adder_1_out), .cin(cin), .cout(adder_1_cout));
  Adder #(.width(18)) adder_2 (.a(B), .b(A), .out(adder_2_out), .cin(cin), .cout(adder_2_cout));
  or OR_2 (OR_2_out, comparator_1_gt, comparator_1_lt);
  or or_3 (or_3_out, adder_1_cout, adder_2_cout);
  Multiplexer #(.select(4), .width(18)) multiplexer_2 (
    .in1(adder_1_out), .in2(OR_out), .in3(adder_2_out), .in4({18{1'b0}}), .in5({18{1'b0}}), .in6(ANDi_out),
    .in7(shifter_1_out), .in8({18{1'b0}}), .in9(adder_2_out), .in10(adder_2_out), .out(result),
    .sel(Selection_bit));  // open: in0, in11, in12, in13, in14, in15, en
  nor nor_1 (nor_1_out, OR_2_out, OR_2_out);
  Multiplexer #(.select(4)) multiplexer_3 (
    .in0(1'b0), .in1(or_3_out), .in2(1'b0), .in3(1'b0), .in4(1'b0), .in5(1'b0), .in6(1'b0), .in7(1'b0),
    .in8(1'b0), .in9(1'b0), .in10(or_3_out), .in11(1'b0), .in12(1'b0), .in13(1'b0), .in14(1'b0), .in15(1'b0),
    .out(cout), .sel(Selection_bit));  // open: en
  Multiplexer multiplexer_4 (.in0(nor_1_out), .in1(comparator_1_eq), .out(Zero_Flag), .sel(OR_2_out));  // open: en

  // Notes on the sheet:
  //   SLL
  //   sub
  //   SUBi/ADD
  //   add
  //   18 bits ALU
  //   Atahar Hossain 2231877642
  //   Sadman Sakib 2232058042
endmodule
